// Logisim project Combinational_Circuit.circ as structural Verilog: 28 circuits, main circuit Half_Adder
module Half_Adder (
  input  x,
  input  y,
  input  x_2,
  input  y_2,
  input  x_3,
  input  y_3,
  output c,
  output s,
  output s_2,
  output c_2,
  output s_3,
  output c_3
);

  wire and_1_out, and_2_out, and_6_out, not_1_out, not_2_out, not_3_out, not_4_out, not_6_out, not_7_out,
       or_1_out, or_2_out, or_4_out;

  not not_1 (not_1_out, y);
  not not_2 (not_2_out, x);
  not not_3 (not_3_out, y_3);
  not not_4 (not_4_out, x_3);
  and and_1 (and_1_out, x, not_1_out);
  and and_2 (and_2_out, y, not_2_out);
  and and_3 (c_2, y, x);
  or or_1 (or_1_out, y_3, x_3);
  or or_2 (or_2_out, not_3_out, not_4_out);
  or or_3 (s, and_1_out, and_2_out);
  and and_4 (s_3, or_1_out, or_2_out);
  not not_5 (c_3, or_2_out);
  not not_6 (not_6_out, y_2);
  not not_7 (not_7_out, x_2);
  and and_5 (c, y_2, x_2);
  and and_6 (and_6_out, not_6_out, not_7_out);
  or or_4 (or_4_out, c, and_6_out);
  not not_8 (s_2, or_4_out);

  // Notes on the sheet:
  //   Best Implementation
  //   Half Adder
endmodule

module Full_Adder (
  input  x,
  input  y,
  input  in_3,
  output s,
  output c
);

  wire and_1_out, and_2_out, not_1_out, not_2_out, not_3_out, not_4_out, not_5_out, or_1_out, or_2_out,
       or_3_out, or_4_out;

  not not_1 (not_1_out, y);
  not not_2 (not_2_out, x);
  or or_1 (or_1_out, y, x);
  or or_2 (or_2_out, not_1_out, not_2_out);
  and and_1 (and_1_out, or_1_out, or_2_out);
  not not_3 (not_3_out, or_2_out);
  and and_2 (and_2_out, in_3, and_1_out);
  not not_4 (not_4_out, and_1_out);
  not not_5 (not_5_out, in_3);
  or or_3 (or_3_out, in_3, and_1_out);
  or or_4 (or_4_out, not_4_out, not_5_out);
  and and_3 (s, or_3_out, or_4_out);
  or or_5 (c, and_2_out, not_3_out);

  // Notes on the sheet:
  //   Full Adder
endmodule

module Parallel_Adder (
  input  B3,
  input  A3,
  input  B2,
  input  A2,
  input  B1,
  input  A1,
  input  B0,
  input  A0,
  input  C0,
  output C4,
  output Y3,
  output Y2,
  output Y1,
  output Y0
);

  wire full_adder_2_c, full_adder_3_c, full_adder_4_c;

  Full_Adder full_adder_1 (.in_3(full_adder_2_c), .s(Y3), .c(C4), .x(B3), .y(A3));
  Full_Adder full_adder_2 (.in_3(full_adder_3_c), .s(Y2), .c(full_adder_2_c), .x(B2), .y(A2));
  Full_Adder full_adder_3 (.in_3(full_adder_4_c), .s(Y1), .c(full_adder_3_c), .x(B1), .y(A1));
  Full_Adder full_adder_4 (.in_3(C0), .s(Y0), .c(full_adder_4_c), .x(B0), .y(A0));

  // Notes on the sheet:
  //   Parallel Adder
endmodule

module _4_Bit_Adder___Subtractor (
  input  C0,
  input  A3,
  input  B3,
  input  A2,
  input  B2,
  input  A1,
  input  B1,
  input  A0,
  input  B0,
  output C4,
  output Y3,
  output Y2,
  output Y1,
  output Y0
);

  wire full_adder_2_c, full_adder_3_c, full_adder_4_c, xor_1_out, xor_2_out, xor_3_out, xor_4_out;

  Full_Adder full_adder_1 (.in_3(full_adder_2_c), .s(Y3), .c(C4), .x(A3), .y(xor_1_out));
  xor xor_1 (xor_1_out, C0, B3);
  Full_Adder full_adder_2 (.in_3(full_adder_3_c), .s(Y2), .c(full_adder_2_c), .x(A2), .y(xor_2_out));
  xor xor_2 (xor_2_out, C0, B2);
  xor xor_3 (xor_3_out, C0, B1);
  Full_Adder full_adder_3 (.in_3(full_adder_4_c), .s(Y1), .c(full_adder_3_c), .x(A1), .y(xor_3_out));
  Full_Adder full_adder_4 (.in_3(C0), .s(Y0), .c(full_adder_4_c), .x(A0), .y(xor_4_out));
  xor xor_4 (xor_4_out, C0, B0);

  // Notes on the sheet:
  //   4-Bit Adder/Subtractor 
endmodule

module Half_Subtractor (
  input  X,
  input  Y,
  output D,
  output B
);

  wire and_1_out, not_1_out, not_2_out;

  not not_1 (not_1_out, Y);
  not not_2 (not_2_out, X);
  and and_1 (and_1_out, X, not_1_out);
  and and_2 (B, Y, not_2_out);
  or or_1 (D, and_1_out, B);

  // Notes on the sheet:
  //   Half Subtractor
endmodule

module Full_Subtractor (
  input  X,
  input  Y,
  input  Z,
  output D,
  output B
);

  wire and_1_out, half_subtractor_1_b, half_subtractor_1_d, not_1_out;

  Half_Subtractor half_subtractor_1 (.D(half_subtractor_1_d), .B(half_subtractor_1_b), .X(X), .Y(Y));
  Half_Subtractor half_subtractor_2 (.D(D), .X(Z), .Y(half_subtractor_1_d));  // open: B
  not not_1 (not_1_out, half_subtractor_1_d);
  and and_1 (and_1_out, Z, not_1_out);
  or or_1 (B, and_1_out, half_subtractor_1_b);

  // Notes on the sheet:
  //   Full Subtractor
endmodule

module Excess_3_Code_Convertor (
  input  A3,
  input  A2,
  input  A1,
  input  A0,
  input  A,
  input  B,
  input  C,
  input  D,
  output out_9,
  output out_10,
  output out_11,
  output out_12,
  output out_13,
  output out_14,
  output out_15,
  output out_16,
  output out_17
);

  wire and_1_out, and_2_out, and_3_out, and_4_out, not_1_out, not_3_out, or_1_out;

  not not_1 (not_1_out, B);
  or or_1 (or_1_out, C, D);
  not not_2 (out_17, D);
  and and_1 (and_1_out, B, or_1_out);
  and and_2 (and_2_out, C, D);
  not not_3 (not_3_out, or_1_out);
  Parallel_Adder parallel_adder_1 (
    .B3(A3), .A3(1'b0), .B2(A2), .A2(1'b0), .B1(A1), .A1(1'b1), .B0(A0), .A0(1'b1), .C4(out_9), .Y3(out_10),
    .Y2(out_11), .Y1(out_12), .Y0(out_13), .C0(1'b0));
  or or_2 (out_14, A, and_1_out);
  and and_3 (and_3_out, not_1_out, or_1_out);
  or or_3 (out_16, and_2_out, not_3_out);
  and and_4 (and_4_out, B, not_3_out);
  or or_4 (out_15, and_4_out, and_3_out);

  // Notes on the sheet:
  //   Excess-3 Code Converter Using Parallel Adder
  //   Excess-3 Code Converter Using K-Map
endmodule

module BCD_Sum_Circuit (
  input  A3,
  input  A2,
  input  A1,
  input  A0,
  input  B3,
  input  B2,
  input  B1,
  input  B0,
  input  C0,
  output Y4,
  output Y3,
  output Y2,
  output Y1,
  output Y0
);

  wire and_1_out, and_2_out, parallel_adder_1_c4, parallel_adder_1_y0, parallel_adder_1_y1,
       parallel_adder_1_y2, parallel_adder_1_y3;

  Parallel_Adder parallel_adder_1 (
    .B3(A3), .A3(B3), .B2(A2), .A2(B2), .B1(A1), .A1(B1), .B0(A0), .A0(B0), .C4(parallel_adder_1_c4),
    .Y3(parallel_adder_1_y3), .Y2(parallel_adder_1_y2), .Y1(parallel_adder_1_y1), .Y0(parallel_adder_1_y0),
    .C0(C0));
  and and_1 (and_1_out, parallel_adder_1_y3, parallel_adder_1_y2);
  and and_2 (and_2_out, parallel_adder_1_y3, parallel_adder_1_y1);
  or or_1 (Y4, parallel_adder_1_c4, and_1_out, and_2_out);
  Parallel_Adder parallel_adder_2 (
    .B3(parallel_adder_1_y3), .A3(1'b0), .B2(parallel_adder_1_y2), .A2(Y4), .B1(parallel_adder_1_y1),
    .A1(Y4), .B0(parallel_adder_1_y0), .A0(1'b0), .Y3(Y3), .Y2(Y2), .Y1(Y1), .Y0(Y0), .C0(1'b0));  // open: C4

  // Notes on the sheet:
  //   BCD Sum Circuit
endmodule

module _4_Bit_Magnitude_Comparartor (
  input  A3,
  input  B3,
  input  A2,
  input  B2,
  input  A1,
  input  B1,
  input  A0,
  input  B0,
  output A_B,
  output A_B_2,
  output A_B_3
);

  wire and_1_out, and_2_out, n2_bit_magnitude_comparator_1_a_b, n2_bit_magnitude_comparator_1_a_b_2,
       n2_bit_magnitude_comparator_1_a_b_3, n2_bit_magnitude_comparator_2_a_b,
       n2_bit_magnitude_comparator_2_a_b_2, n2_bit_magnitude_comparator_2_a_b_3;

  _2_Bit_Magnitude_Comparator u_2_bit_magnitude_comparator_1 (
    .A_B(n2_bit_magnitude_comparator_1_a_b), .A_B_2(n2_bit_magnitude_comparator_1_a_b_2),
    .A_B_3(n2_bit_magnitude_comparator_1_a_b_3), .A1(A3), .B1(B3), .A0(A2), .B0(B2));
  and and_1 (and_1_out, n2_bit_magnitude_comparator_1_a_b_3, n2_bit_magnitude_comparator_2_a_b_2);
  _2_Bit_Magnitude_Comparator u_2_bit_magnitude_comparator_2 (
    .A_B(n2_bit_magnitude_comparator_2_a_b), .A_B_2(n2_bit_magnitude_comparator_2_a_b_2),
    .A_B_3(n2_bit_magnitude_comparator_2_a_b_3), .A1(A1), .B1(B1), .A0(A0), .B0(B0));
  and and_2 (and_2_out, n2_bit_magnitude_comparator_1_a_b_3, n2_bit_magnitude_comparator_2_a_b);
  and and_3 (A_B, n2_bit_magnitude_comparator_2_a_b_3, n2_bit_magnitude_comparator_1_a_b_3);
  or or_1 (A_B_2, and_1_out, n2_bit_magnitude_comparator_1_a_b_2);
  or or_2 (A_B_3, and_2_out, n2_bit_magnitude_comparator_1_a_b);

  // Notes on the sheet:
  //   4-Bit Magnitude Comparator
endmodule

module _1_Bit_Magnitude_Comparator (
  input  A,
  input  B,
  output A_B,
  output A_B_2,
  output A_B_3
);

  wire and_2_out, and_3_out, not_1_out, not_2_out;

  and and_1 (A_B, A, not_2_out);
  and and_2 (and_2_out, A, B);
  or or_1 (A_B_2, and_2_out, and_3_out);
  not not_1 (not_1_out, A);
  and and_3 (and_3_out, not_1_out, not_2_out);
  and and_4 (A_B_3, B, not_1_out);
  not not_2 (not_2_out, B);

  // Notes on the sheet:
  //   1-Bit Magnitude Comparator
endmodule

module _2_Bit_Magnitude_Comparator (
  input  A1,
  input  B1,
  input  A0,
  input  B0,
  output A_B,
  output A_B_2,
  output A_B_3
);

  wire and_1_out, and_2_out, n1_bit_magnitude_comparator_1_a_b, n1_bit_magnitude_comparator_1_a_b_2,
       n1_bit_magnitude_comparator_1_a_b_3, n1_bit_magnitude_comparator_2_a_b,
       n1_bit_magnitude_comparator_2_a_b_2, n1_bit_magnitude_comparator_2_a_b_3;

  _1_Bit_Magnitude_Comparator u_1_bit_magnitude_comparator_1 (
    .A(A1), .B(B1), .A_B(n1_bit_magnitude_comparator_1_a_b), .A_B_2(n1_bit_magnitude_comparator_1_a_b_2),
    .A_B_3(n1_bit_magnitude_comparator_1_a_b_3));
  _1_Bit_Magnitude_Comparator u_1_bit_magnitude_comparator_2 (
    .A(A0), .B(B0), .A_B(n1_bit_magnitude_comparator_2_a_b), .A_B_2(n1_bit_magnitude_comparator_2_a_b_2),
    .A_B_3(n1_bit_magnitude_comparator_2_a_b_3));
  and and_1 (and_1_out, n1_bit_magnitude_comparator_2_a_b, n1_bit_magnitude_comparator_1_a_b_2);
  and and_2 (and_2_out, n1_bit_magnitude_comparator_1_a_b_2, n1_bit_magnitude_comparator_2_a_b_3);
  or or_1 (A_B, and_2_out, n1_bit_magnitude_comparator_1_a_b_3);
  or or_2 (A_B_2, n1_bit_magnitude_comparator_1_a_b, and_1_out);
  and and_3 (A_B_3, n1_bit_magnitude_comparator_2_a_b_2, n1_bit_magnitude_comparator_1_a_b_2);

  // Notes on the sheet:
  //   2-Bit Magnitude Comparator
endmodule

module _3X8_Decoder (
  input  S2,
  input  S1,
  input  S0,
  input  E,
  output Y7,
  output Y6,
  output Y5,
  output Y4,
  output Y3,
  output Y2,
  output Y1,
  output Y0
);

  wire not_1_out, not_2_out, not_3_out, not_4_out;

  not not_1 (not_1_out, S2);
  not not_2 (not_2_out, S1);
  not not_3 (not_3_out, S0);
  not not_4 (not_4_out, E);
  and and_1 (Y7, S2, S1, S0, not_4_out);
  and and_2 (Y6, S2, S1, not_3_out, not_4_out);
  and and_3 (Y5, S2, not_2_out, S0, not_4_out);
  and and_4 (Y4, S2, not_2_out, not_3_out, not_4_out);
  and and_5 (Y3, not_1_out, S1, S0, not_4_out);
  and and_6 (Y2, not_1_out, S1, not_3_out, not_4_out);
  and and_7 (Y1, not_1_out, not_2_out, S0, not_4_out);
  and and_8 (Y0, not_1_out, not_2_out, not_3_out, not_4_out);

  // Notes on the sheet:
  //   3X8 Decoder
endmodule

module _1X2_Demultiplexer (
  input  S,
  input  A,
  output A1,
  output A0
);

  wire not_1_out;

  not not_1 (not_1_out, S);
  and and_1 (A1, S, A);
  and and_2 (A0, A, not_1_out);

  // Notes on the sheet:
  //   1x2 Demultiplexer
endmodule

module _1X4_Demultiplexer (
  input  A,
  input  S0,
  input  S1,
  output Y0,
  output Y1,
  output Y2,
  output Y3
);

  wire n1x2_demultiplexer_1_a0, n1x2_demultiplexer_1_a1;

  _1X2_Demultiplexer u_1x2_demultiplexer_1 (.S(S1), .A(A), .A1(n1x2_demultiplexer_1_a1), .A0(n1x2_demultiplexer_1_a0));
  _1X2_Demultiplexer u_1x2_demultiplexer_2 (.S(S0), .A(n1x2_demultiplexer_1_a0), .A1(Y1), .A0(Y0));
  _1X2_Demultiplexer u_1x2_demultiplexer_3 (.S(S0), .A(n1x2_demultiplexer_1_a1), .A1(Y3), .A0(Y2));

  // Notes on the sheet:
  //   1x4 Demultiplexer Using 1X2 Demultiplexer
endmodule

module _4X16_Decoder (
  input  S2,
  input  S1,
  input  S0,
  input  S3,
  output Y0,
  output Y1,
  output Y2,
  output Y3,
  output Y4,
  output Y5,
  output Y6,
  output Y7,
  output Y8,
  output Y9,
  output Y10,
  output Y11,
  output Y12,
  output Y13,
  output Y14,
  output Y15
);

  wire not_1_out;

  not not_1 (not_1_out, S3);
  _3X8_Decoder u_3x8_decoder_1 (
    .Y7(Y0), .Y6(Y1), .Y5(Y2), .Y4(Y3), .Y3(Y4), .Y2(Y5), .Y1(Y6), .Y0(Y7), .S2(S2), .S1(S1), .S0(S0), .E(S3));
  _3X8_Decoder u_3x8_decoder_2 (
    .Y7(Y8), .Y6(Y9), .Y5(Y10), .Y4(Y11), .Y3(Y12), .Y2(Y13), .Y1(Y14), .Y0(Y15), .S2(S2), .S1(S1), .S0(S0),
    .E(not_1_out));

  // Notes on the sheet:
  //   4X16 Decoder Using 3X8 Decoder
endmodule

module _2x1_Multiplexer (
  input  A,
  input  S,
  input  B,
  input  E,
  output Y
);

  wire and_1_out, and_2_out, not_1_out, not_2_out;

  not not_1 (not_1_out, E);
  not not_2 (not_2_out, S);
  and and_1 (and_1_out, A, not_1_out, not_2_out);
  and and_2 (and_2_out, S, not_1_out, B);
  or or_1 (Y, and_1_out, and_2_out);

  // Notes on the sheet:
  //   2X1 Multiplexer
endmodule

module _4X1_Multilpexer (
  input  A0,
  input  A2,
  input  S1,
  input  E,
  input  A1,
  input  A3,
  input  S0,
  output Y
);

  wire n2x1_multiplexer_1_y, n2x1_multiplexer_2_y;

  _2x1_Multiplexer u_2x1_multiplexer_1 (.A(A0), .S(S1), .B(A2), .Y(n2x1_multiplexer_1_y), .E(E));
  _2x1_Multiplexer u_2x1_multiplexer_2 (.A(A1), .S(S1), .B(A3), .Y(n2x1_multiplexer_2_y), .E(E));
  _2x1_Multiplexer u_2x1_multiplexer_3 (.A(n2x1_multiplexer_1_y), .S(S0), .B(n2x1_multiplexer_2_y), .Y(Y), .E(E));

  // Notes on the sheet:
  //   4X1 Multiplexer Using 2X1 Multiplexer
endmodule

module _8X1_Multiplexer (
  input  A0,
  input  A1,
  input  A2,
  input  A3,
  input  S1,
  input  S0,
  input  E,
  input  A4,
  input  A5,
  input  A6,
  input  S2,
  input  A7,
  output Y
);

  wire n4x1_multilpexer_1_y, n4x1_multilpexer_2_y;

  _4X1_Multilpexer u_4x1_multilpexer_1 (
    .A0(A0), .A2(A2), .S1(S0), .Y(n4x1_multilpexer_1_y), .A1(A1), .A3(A3), .S0(S1), .E(E));
  _4X1_Multilpexer u_4x1_multilpexer_2 (
    .A0(A4), .A2(A6), .S1(S0), .Y(n4x1_multilpexer_2_y), .A1(A5), .A3(A7), .S0(S1), .E(E));
  _2x1_Multiplexer u_2x1_multiplexer_1 (.A(n4x1_multilpexer_1_y), .S(S2), .B(n4x1_multilpexer_2_y), .Y(Y), .E(E));

  // Notes on the sheet:
  //   8X1 Multiplexer Using 4X1 Multiplexer And 2X1 Multiplexer
endmodule

module _2X1_Encoder (
  input  A0,
  input  A0_2,
  input  A1,
  input  A1_2,
  input  E,
  input  E_2,
  output Y,
  output Y_2
);

  wire not_1_out, not_2_out, not_3_out;

  not not_1 (not_1_out, E);
  not not_2 (not_2_out, A0);
  and and_1 (Y, not_2_out, not_1_out, A1);
  not not_3 (not_3_out, E_2);
  and and_2 (Y_2, not_3_out, A1_2);

  // Notes on the sheet:
  //   Low Priority Encoder
  //   2X1 Encoder
  //   High Priority Encoder
endmodule

module _4X2_Encoder (
  input  D3,
  input  D3_2,
  input  D2,
  input  D2_2,
  input  D1,
  input  D1_2,
  input  D0,
  input  D0_2,
  input  D3_3,
  input  D2_3,
  input  D1_3,
  input  D0_3,
  output X,
  output X_2,
  output Y,
  output Y_2,
  output X_3,
  output Y_3
);

  wire and_1_out, and_2_out, and_3_out, and_4_out, and_5_out, not_1_out, not_2_out, not_3_out, not_4_out,
       not_5_out;

  or or_1 (X, D3, D2_2);
  or or_2 (Y, D3, D1);
  not not_1 (not_1_out, D2_3);
  not not_2 (not_2_out, D1_3);
  not not_3 (not_3_out, D0_3);
  and and_1 (and_1_out, D3_3, not_1_out, not_2_out, not_3_out);
  and and_2 (and_2_out, D1_3, not_3_out);
  and and_3 (and_3_out, D2_3, not_3_out, not_2_out);
  not not_4 (not_4_out, D3_2);
  not not_5 (not_5_out, D2);
  and and_4 (and_4_out, D1_2, not_5_out, not_4_out);
  and and_5 (and_5_out, D2, not_4_out);
  or or_3 (X_3, and_1_out, and_3_out);
  or or_4 (Y_3, and_1_out, and_2_out);
  or or_5 (X_2, D3_2, and_5_out);
  or or_6 (Y_2, D3_2, and_4_out);

  // Notes on the sheet:
  //   Normal Encoder
  //   Low Priority Encoder
  //   4X2 Encoder
  //   High Priority Encoder
endmodule

module Quadruple_2_to_1_Line_Multiplexer (
  input  A0,
  input  B0,
  input  A1,
  input  B1,
  input  S,
  input  E,
  input  A2,
  input  B2,
  input  A3,
  input  B3,
  output Y0,
  output Y1,
  output Y2,
  output Y3
);

  _2x1_Multiplexer u_2x1_multiplexer_1 (.A(A0), .S(S), .B(B0), .Y(Y0), .E(E));
  _2x1_Multiplexer u_2x1_multiplexer_2 (.A(A1), .S(S), .B(B1), .Y(Y1), .E(E));
  _2x1_Multiplexer u_2x1_multiplexer_3 (.A(A2), .S(S), .B(B2), .Y(Y2), .E(E));
  _2x1_Multiplexer u_2x1_multiplexer_4 (.A(A3), .S(S), .B(B3), .Y(Y3), .E(E));

  // Notes on the sheet:
  //   Quadruple 2 to 1 Line Multiplexer
endmodule

module _3_Bit_Odd_Parity_Generator_Checker (
  input  x,
  input  y,
  input  z,
  input  x_2,
  input  y_2,
  input  z_2,
  input  P,
  output P_2,
  output C
);

  wire xnor_1_out, xnor_2_out, xor_1_out;

  xor xor_1 (xor_1_out, x, y);
  xnor xnor_1 (xnor_1_out, x_2, y_2);
  xnor xnor_2 (xnor_2_out, z_2, P);
  xnor xnor_3 (P_2, xor_1_out, z);
  xnor xnor_4 (C, xnor_1_out, xnor_2_out);

  // Notes on the sheet:
  //   3 Bit Odd Parity Generator
  //   3 Bit Odd Parity Checker
  //   Odd Parity Generator/Checker
endmodule

module Carry_Look_Ahead_Adder (
  input  P3,
  input  G3,
  input  P2,
  input  G2,
  input  P1,
  input  G1,
  input  P0,
  input  G0,
  input  C0,
  output C4,
  output C3,
  output C2,
  output C1
);

  wire and_1_out, and_2_out, and_3_out, and_4_out, and_5_out, and_6_out, and_7_out, and_8_out, and_9_out,
       and_10_out;

  and and_1 (and_1_out, P3, P2, P1, P0, C0);
  and and_2 (and_2_out, P3, P2, P1, G0);
  and and_3 (and_3_out, P3, P2, G1);
  and and_4 (and_4_out, P3, G2);
  and and_5 (and_5_out, P0, P1, P2, C0);
  and and_6 (and_6_out, G0, P1, P2);
  and and_7 (and_7_out, G1, P2);
  and and_8 (and_8_out, P1, P0, C0);
  and and_9 (and_9_out, G0, P1);
  and and_10 (and_10_out, P0, C0);
  or or_1 (C4, and_1_out, and_2_out, and_3_out, and_4_out, G3);
  or or_2 (C3, and_5_out, and_6_out, and_7_out, G2);
  or or_3 (C2, and_8_out, and_9_out, G1);
  or or_4 (C1, and_10_out, G0);
endmodule

module Adder_for_CLA (
  input  A,
  input  B,
  output P,
  output G
);

  and and_1 (G, A, B);
  xor xor_1 (P, A, B);

  // Notes on the sheet:
  //   Propagation / Generation Generator
  //   P indicate Propagation and G indicate Generation
endmodule

module _4_Bit_CLA (
  input  A3,
  input  B3,
  input  A2,
  input  B2,
  input  A1,
  input  B1,
  input  A0,
  input  B0,
  input  C0,
  output C4,
  output S3,
  output S2,
  output S1,
  output S0
);

  wire adder_for_cla_1_g, adder_for_cla_1_p, adder_for_cla_2_g, adder_for_cla_2_p, adder_for_cla_3_g,
       adder_for_cla_3_p, adder_for_cla_4_g, adder_for_cla_4_p, carry_look_ahead_adder_1_c1,
       carry_look_ahead_adder_1_c2, carry_look_ahead_adder_1_c3;

  Adder_for_CLA adder_for_cla_1 (.A(A3), .B(B3), .P(adder_for_cla_1_p), .G(adder_for_cla_1_g));
  Adder_for_CLA adder_for_cla_2 (.A(A2), .B(B2), .P(adder_for_cla_2_p), .G(adder_for_cla_2_g));
  Adder_for_CLA adder_for_cla_3 (.A(A1), .B(B1), .P(adder_for_cla_3_p), .G(adder_for_cla_3_g));
  Adder_for_CLA adder_for_cla_4 (.A(A0), .B(B0), .P(adder_for_cla_4_p), .G(adder_for_cla_4_g));
  Carry_Look_Ahead_Adder carry_look_ahead_adder_1 (
    .C3(carry_look_ahead_adder_1_c3), .P2(adder_for_cla_2_p), .G2(adder_for_cla_2_g),
    .C2(carry_look_ahead_adder_1_c2), .P1(adder_for_cla_3_p), .G1(adder_for_cla_3_g), .P0(adder_for_cla_4_p),
    .C1(carry_look_ahead_adder_1_c1), .G0(adder_for_cla_4_g), .C0(C0), .P3(adder_for_cla_1_p),
    .G3(adder_for_cla_1_g), .C4(C4));
  xor xor_1 (S3, adder_for_cla_1_p, carry_look_ahead_adder_1_c3);
  xor xor_2 (S2, adder_for_cla_2_p, carry_look_ahead_adder_1_c2);
  xor xor_3 (S1, adder_for_cla_3_p, carry_look_ahead_adder_1_c1);
  xor xor_4 (S0, C0, adder_for_cla_4_p);

  // Notes on the sheet:
  //   4-Bit Carry Look Ahead Adder
endmodule

module _16_Bit_Adder_Using_4_Bit_CLA (
  input  A15,
  input  A14,
  input  A13,
  input  A12,
  input  B15,
  input  B14,
  input  B13,
  input  B12,
  input  A11,
  input  A10,
  input  A9,
  input  A8,
  input  B11,
  input  B10,
  input  B9,
  input  B8,
  input  A7,
  input  A6,
  input  A5,
  input  A4,
  input  B7,
  input  B6,
  input  B5,
  input  B4,
  input  A3,
  input  A2,
  input  A1,
  input  A0,
  input  B3,
  input  B2,
  input  B1,
  input  B0,
  output Y16,
  output Y15,
  output Y14,
  output Y13,
  output Y12,
  output Y11,
  output Y10,
  output Y9,
  output Y8,
  output Y7,
  output Y6,
  output Y5,
  output Y4,
  output Y3,
  output Y2,
  output Y1,
  output Y0
);

  wire n4_bit_cla_2_c4, n4_bit_cla_3_c4, n4_bit_cla_4_c4;

  _4_Bit_CLA u_4_bit_cla_1 (
    .A3(A15), .B3(B15), .A2(A14), .B2(B14), .A1(A13), .B1(B13), .A0(A12), .B0(B12), .C0(n4_bit_cla_2_c4),
    .C4(Y16), .S3(Y15), .S2(Y14), .S1(Y13), .S0(Y12));
  _4_Bit_CLA u_4_bit_cla_2 (
    .A3(A11), .B3(B11), .A2(A10), .B2(B10), .A1(A9), .B1(B9), .A0(A8), .B0(B8), .C0(n4_bit_cla_3_c4),
    .C4(n4_bit_cla_2_c4), .S3(Y11), .S2(Y10), .S1(Y9), .S0(Y8));
  _4_Bit_CLA u_4_bit_cla_3 (
    .A3(A7), .B3(B7), .A2(A6), .B2(B6), .A1(A5), .B1(B5), .A0(A4), .B0(B4), .C0(n4_bit_cla_4_c4),
    .C4(n4_bit_cla_3_c4), .S3(Y7), .S2(Y6), .S1(Y5), .S0(Y4));
  _4_Bit_CLA u_4_bit_cla_4 (
    .A3(A3), .B3(B3), .A2(A2), .B2(B2), .A1(A1), .B1(B1), .A0(A0), .B0(B0), .C0(1'b0), .C4(n4_bit_cla_4_c4),
    .S3(Y3), .S2(Y2), .S1(Y1), .S0(Y0));

  // Notes on the sheet:
  //   16 -Bit Adder Using 4-Bit Carry Look Ahead Adder Circuit 
endmodule

module _1x8_Demultiplexer (
  input  INPUT,
  input  S2,
  input  S1,
  input  S0,
  output Y0,
  output Y1,
  output Y2,
  output Y3,
  output Y4,
  output Y5,
  output Y6,
  output Y7
);

  wire n1x2_demultiplexer_1_a0, n1x2_demultiplexer_1_a1;

  _1X2_Demultiplexer u_1x2_demultiplexer_1 (
    .S(S2), .A(INPUT), .A1(n1x2_demultiplexer_1_a1), .A0(n1x2_demultiplexer_1_a0));
  _1X4_Demultiplexer u_1x4_demultiplexer_1 (
    .A(n1x2_demultiplexer_1_a0), .S0(S1), .S1(S0), .Y0(Y0), .Y1(Y1), .Y2(Y2), .Y3(Y3));
  _1X4_Demultiplexer u_1x4_demultiplexer_2 (
    .A(n1x2_demultiplexer_1_a1), .S0(S1), .S1(S0), .Y0(Y4), .Y1(Y5), .Y2(Y6), .Y3(Y7));

  // Notes on the sheet:
  //   1X8 Demultiplexer Using 1X4 Demultiplexer and 1X2 Demultiplexer
endmodule

module _3_Bit_Even_Parity_Generator_Checker (
  input  x,
  input  y,
  input  z,
  input  x_2,
  input  y_2,
  input  z_2,
  input  P,
  output P_2,
  output C
);

  wire xnor_1_out, xnor_2_out, xor_1_out;

  xor xor_1 (xor_1_out, x, y);
  xnor xnor_1 (xnor_1_out, x_2, y_2);
  xnor xnor_2 (xnor_2_out, z_2, P);
  xor xor_2 (P_2, xor_1_out, z);
  xor xor_3 (C, xnor_1_out, xnor_2_out);

  // Notes on the sheet:
  //   3 Bit Even Parity Generator
  //   3 Bit Even Parity Checker
  //   Even Parity Generator/Checker
endmodule
