// Logisim project Full Subtractor Implementation.circ as structural Verilog
module Half_Subtractor (
  input  X,
  input  Y,
  output D,
  output B
);

  wire not_1_out;

  not not_1 (not_1_out, X);
  and and_1 (B, not_1_out, Y);
  xor xor_1 (D, X, Y);

  // Notes on the sheet:
  //   Half Subtractor Using XOR and AND Gates
  //   D is Difference and B is Borrow and We are doing X-Y
endmodule

module Full_Subtractor (
  input  X,
  input  Y,
  input  Z,
  output D,
  output B
);

  wire and_1_out, half_subtractor_1_b, half_subtractor_1_d, not_1_out;

  Half_Subtractor half_subtractor_1 (.X(X), .Y(Y), .D(half_subtractor_1_d), .B(half_subtractor_1_b));
  not not_1 (not_1_out, half_subtractor_1_d);
  and and_1 (and_1_out, Z, not_1_out);
  Half_Subtractor half_subtractor_2 (.X(half_subtractor_1_d), .Y(Z), .D(D));  // open: B
  or or_1 (B, and_1_out, half_subtractor_1_b);

  // Notes on the sheet:
  //   Ful Subtractor Using Two Half Subtractors and Mix of OR and And Gates
  //   D is Difference and B is Borrow and We are doing X-Y-Z
endmodule

module Full_Subtractor_Using_Nand_Gates (
  input  X,
  input  Y,
  input  Z,
  output D,
  output B
);

  wire nand_1_out, nand_2_out, nand_3_out, nand_4_out, nand_5_out, nand_6_out, nand_7_out;

  nand nand_1 (nand_1_out, X, Y);
  nand nand_2 (nand_2_out, X, nand_1_out);
  nand nand_3 (nand_3_out, nand_1_out, Y);
  nand nand_4 (nand_4_out, nand_2_out, nand_3_out);
  nand nand_5 (nand_5_out, nand_4_out, Z);
  nand nand_6 (nand_6_out, nand_4_out, nand_5_out);
  nand nand_7 (nand_7_out, nand_5_out, Z);
  nand nand_8 (D, nand_6_out, nand_7_out);
  nand nand_9 (B, nand_7_out, nand_3_out);

  // Notes on the sheet:
  //   Full Subtractor Using Minimum Number of NAND Gates
  //   D is Difference and B is Borrow and We are doing X-Y-Z
endmodule
