// Logisim project Finite State Machine.circ as structural Verilog: 2 circuits, main circuit JK Flip Flop
module JK_Flip_Flop (
  input  J,
  input  CP,
  input  K,
  input  CLEAR_prime,
  output Q,
  output Q_prime
);

  wire nand_1_out, nand_2_out, nand_3_out, nand_4_out, nand_5_out, nand_6_out, not_1_out;

  not not_1 (not_1_out, CP);
  nand nand_1 (nand_1_out, Q_prime, J, CP);
  nand nand_2 (nand_2_out, CP, K, Q);
  nand nand_3 (nand_3_out, nand_1_out, nand_4_out);
  nand nand_4 (nand_4_out, nand_3_out, CLEAR_prime, nand_2_out);
  nand nand_5 (nand_5_out, nand_3_out, not_1_out);
  nand nand_6 (nand_6_out, not_1_out, nand_4_out);
  nand nand_7 (Q, nand_5_out, Q_prime);
  nand nand_8 (Q_prime, Q, CLEAR_prime, nand_6_out);

  // Notes on the sheet:
  //   Negative Edge Triggered Master Slave JK Flip-Flop With Active Low Clear
endmodule

module FSM_Finite_State_Machine (
  input  C,
  input  CP,
  input  Clear_prime,
  output Y
);

  wire jk_flip_flop_1_q_prime, nand_1_out, nand_2_out, nand_3_out;

  nand nand_1 (nand_1_out, CP, CP);
  nand nand_2 (nand_2_out, C, C);
  JK_Flip_Flop jk_flip_flop_1 (
    .J(C), .CP(nand_1_out), .K(nand_2_out), .CLEAR_prime(Clear_prime), .Q_prime(jk_flip_flop_1_q_prime));  // open: Q
  nand nand_3 (nand_3_out, C, jk_flip_flop_1_q_prime);
  nand nand_4 (Y, nand_3_out, nand_3_out);

  // Notes on the sheet:
  //   Finite State Machine that Detect Positive Edge
endmodule
