// Logisim project PYQcircuits.circ as structural Verilog: 2 circuits, main circuit 4bit_BinaryToBCD_Converter
module _4bit_BinaryToBCD_Converter (
  input  A3,
  input  A2,
  input  A1,
  input  A0,
  output Y4,
  output Y3,
  output Y2,
  output Y1,
  output Y0
);

  wire and_1_out, and_2_out, and_4_out, and_5_out, and_6_out, and_7_out, not_1_out, not_2_out, not_3_out;

  not not_1 (not_1_out, A3);
  not not_2 (not_2_out, A2);
  not not_3 (not_3_out, A1);
  and and_1 (and_1_out, A3, A2);
  and and_2 (and_2_out, A3, A1);
  and and_3 (Y3, A3, not_2_out, not_3_out);
  and and_4 (and_4_out, not_1_out, A2);
  and and_5 (and_5_out, A1, A2);
  and and_6 (and_6_out, A3, A2, not_3_out);
  and and_7 (and_7_out, not_1_out, A1);
  or or_1 (Y4, and_1_out, and_2_out);
  or or_2 (Y2, and_4_out, and_5_out);
  or or_3 (Y1, and_6_out, and_7_out);

  assign Y0 = A0;

  // Notes on the sheet:
  //   Binary to BCD Converter
endmodule

module _4Bit_Binary_To_Gray_Code (
  input  A3,
  input  A2,
  input  A1,
  input  A0,
  output Y3,
  output Y2,
  output Y1,
  output Y0
);

  xor xor_1 (Y2, A3, A2);
  xor xor_2 (Y1, A2, A1);
  xor xor_3 (Y0, A1, A0);

  assign Y3 = A3;

  // Notes on the sheet:
  //   Binary to Gray Code Converter
endmodule
