// Logisim project 4x1 MUX Using 2X1 MUX (Using NAND Gates Only).circ as structural Verilog: 2 circuits, main circuit 2X1 MUX Using NAND Gates
module _2X1_MUX_Using_NAND_Gates (
  input  I0,
  input  I1,
  input  S,
  output Y
);

  wire nand_1_out, nand_2_out, nand_3_out;

  nand nand_1 (nand_1_out, S, S);
  nand nand_2 (nand_2_out, I0, nand_1_out);
  nand nand_3 (nand_3_out, I1, S);
  nand nand_4 (Y, nand_2_out, nand_3_out);

  // Notes on the sheet:
  //   2x1 MUX Using NAND Gates
endmodule

module _4x1_MUX_Using_2X1_MUX_Implemented_By_NAND_Gates (
  input  I0,
  input  I2,
  input  I1,
  input  I3,
  input  S1,
  input  S0,
  output Y
);

  wire n2x1_mux_using_nands_1_y, n2x1_mux_using_nands_2_y;

  _2X1_MUX_Using_NAND_Gates u_2x1_mux_using_nands_1 (.I0(I0), .I1(I2), .S(S1), .Y(n2x1_mux_using_nands_1_y));
  _2X1_MUX_Using_NAND_Gates u_2x1_mux_using_nands_2 (.I0(I1), .I1(I3), .S(S1), .Y(n2x1_mux_using_nands_2_y));
  _2X1_MUX_Using_NAND_Gates u_2x1_mux_using_nands_3 (
    .I0(n2x1_mux_using_nands_1_y), .I1(n2x1_mux_using_nands_2_y), .S(S0), .Y(Y));

  // Notes on the sheet:
  //   4X1 MUX Using three 2X1 MUX
endmodule
