// Logisim project Functional Implementation Using 4X1 MUX.circ as structural Verilog: 3 circuits, main circuit 2x1 MUX
module _2x1_MUX (
  input  A,
  input  S,
  input  B,
  input  E,
  output Y
);

  wire and_1_out, and_2_out, not_1_out, not_2_out;

  not not_1 (not_1_out, E);
  not not_2 (not_2_out, S);
  and and_1 (and_1_out, A, not_1_out, not_2_out);
  and and_2 (and_2_out, S, not_1_out, B);
  or or_1 (Y, and_1_out, and_2_out);

  // Notes on the sheet:
  //   2X1 MUX Using AND, OR Gates With Enable
  //   E is Enable and S is Select Line whereas A and B are Inputs and Y is Output
endmodule

module _4X1_MUX (
  input  I0,
  input  I2,
  input  I1,
  input  I3,
  input  S1,
  input  S0,
  input  E,
  output Y
);

  wire n2x1_mux_1_y, n2x1_mux_2_y;

  _2x1_MUX u_2x1_mux_1 (.A(I0), .S(S1), .B(I2), .E(E), .Y(n2x1_mux_1_y));
  _2x1_MUX u_2x1_mux_2 (.A(I1), .S(S1), .B(I3), .E(E), .Y(n2x1_mux_2_y));
  _2x1_MUX u_2x1_mux_3 (.A(n2x1_mux_1_y), .S(S0), .B(n2x1_mux_2_y), .E(E), .Y(Y));

  // Notes on the sheet:
  //   Data 
  //   Inputs
  //   4X1 MUX Implemented By 2X1 MUX
  //   E is Enable and S1 and S0 are Select Lines and Y is Output
  //   Data 
  //   Outputs
endmodule

module Functional_Implementation_Using_4X1_MUX (
  input  W,
  input  X,
  input  Y,
  input  Z,
  input  E,
  output Y_2
);

  wire xor_1_out, xor_2_out;

  xor xor_1 (xor_1_out, Z, Y);
  xor xor_2 (xor_2_out, xor_1_out, 1'b1);
  _4X1_MUX u_4x1_mux_1 (.I0(xor_1_out), .I2(1'b1), .I1(xor_2_out), .I3(1'b0), .S1(W), .S0(X), .E(E), .Y(Y_2));

  // Notes on the sheet:
  //   Functional Implementation of (1,2,4,7,8,9,10,11) in Sum of Products Form
endmodule
