// Logisim project 2-Bit_Magnitude_Comparator.circ as structural Verilog: 2 circuits, main circuit 1-Bit Magnitude Comparator
module _1_Bit_Magnitude_Comparator (
  input  A,
  input  B,
  output A_B,
  output A_B_2,
  output A_B_3
);

  wire and_2_out, and_3_out, not_1_out, not_2_out;

  and and_1 (A_B, A, not_2_out);
  and and_2 (and_2_out, A, B);
  not not_1 (not_1_out, A);
  and and_3 (and_3_out, not_1_out, not_2_out);
  or or_1 (A_B_2, and_2_out, and_3_out);
  and and_4 (A_B_3, B, not_1_out);
  not not_2 (not_2_out, B);

  // Notes on the sheet:
  //    1-Bit Magnitude Comparator
endmodule

module _2_Bit_Magnitude_Comparator (
  input  A1,
  input  B1,
  input  A0,
  input  B0,
  output A_B,
  output A_B_2,
  output A_B_3
);

  wire and_1_out, and_2_out, n1_bit_magnitude_comparator_1_a_b, n1_bit_magnitude_comparator_1_a_b_2,
       n1_bit_magnitude_comparator_1_a_b_3, n1_bit_magnitude_comparator_2_a_b,
       n1_bit_magnitude_comparator_2_a_b_2, n1_bit_magnitude_comparator_2_a_b_3;

  _1_Bit_Magnitude_Comparator u_1_bit_magnitude_comparator_1 (
    .A(A1), .B(B1), .A_B(n1_bit_magnitude_comparator_1_a_b), .A_B_2(n1_bit_magnitude_comparator_1_a_b_2),
    .A_B_3(n1_bit_magnitude_comparator_1_a_b_3));
  and and_1 (and_1_out, n1_bit_magnitude_comparator_1_a_b_2, n1_bit_magnitude_comparator_2_a_b);
  _1_Bit_Magnitude_Comparator u_1_bit_magnitude_comparator_2 (
    .A(A0), .B(B0), .A_B(n1_bit_magnitude_comparator_2_a_b), .A_B_2(n1_bit_magnitude_comparator_2_a_b_2),
    .A_B_3(n1_bit_magnitude_comparator_2_a_b_3));
  and and_2 (and_2_out, n1_bit_magnitude_comparator_1_a_b_2, n1_bit_magnitude_comparator_2_a_b_3);
  or or_1 (A_B, and_2_out, n1_bit_magnitude_comparator_1_a_b_3);
  or or_2 (A_B_2, n1_bit_magnitude_comparator_1_a_b, and_1_out);
  and and_3 (A_B_3, n1_bit_magnitude_comparator_2_a_b_2, n1_bit_magnitude_comparator_1_a_b_2);

  // Notes on the sheet:
  //   2-Bit Magnitude Comparator Using 1-Bit Magnitude Comparator
endmodule
