// Logisim project AdderSubtractor.circ as structural Verilog: 3 circuits, main circuit Half Adder
module Half_Adder (
  input  A,
  input  B,
  output S,
  output C
);

  xor xor_1 (S, A, B);
  and and_1 (C, A, B);

  // Notes on the sheet:
  //   Half Adder Using Mix of Gates
  //   S is Sum and C is Carry and We are doing A+B
endmodule

module Full_Adder (
  input  A,
  input  B,
  input  C,
  output S,
  output Cout
);

  wire half_adder_1_c, half_adder_1_s, half_adder_2_c;

  Half_Adder half_adder_1 (.A(A), .B(B), .S(half_adder_1_s), .C(half_adder_1_c));
  Half_Adder half_adder_2 (.A(half_adder_1_s), .B(C), .S(S), .C(half_adder_2_c));
  or or_1 (Cout, half_adder_2_c, half_adder_1_c);

  // Notes on the sheet:
  //   Full Adder Using Two Half Adders and Mix Of Gates
  //   S is Sum and Cout is Carry and We are doing A+B+C
endmodule

module _4_Bit_Adder_Subtractor (
  input  B3,
  input  A3,
  input  B2,
  input  A2,
  input  B1,
  input  A1,
  input  B0,
  input  A0,
  input  Add_Sub,
  output C_out,
  output S3,
  output S2,
  output S1,
  output S0
);

  wire full_adder_2_cout, full_adder_3_cout, full_adder_4_cout, xor_1_out, xor_2_out, xor_3_out, xor_4_out;

  xor xor_1 (xor_1_out, B3, Add_Sub);
  Full_Adder full_adder_1 (.A(A3), .B(xor_1_out), .C(full_adder_2_cout), .Cout(C_out), .S(S3));
  xor xor_2 (xor_2_out, B2, Add_Sub);
  Full_Adder full_adder_2 (.A(A2), .B(xor_2_out), .C(full_adder_3_cout), .Cout(full_adder_2_cout), .S(S2));
  xor xor_3 (xor_3_out, B1, Add_Sub);
  Full_Adder full_adder_3 (.A(A1), .B(xor_3_out), .C(full_adder_4_cout), .Cout(full_adder_3_cout), .S(S1));
  xor xor_4 (xor_4_out, B0, Add_Sub);
  Full_Adder full_adder_4 (.A(A0), .B(xor_4_out), .C(Add_Sub), .Cout(full_adder_4_cout), .S(S0));

  // Notes on the sheet:
  //   4-Bit Adder / Subtractor Using 4-Full Adders And XOR Gates
  //   0 For Add and 1 For Subtract
endmodule
