// Logisim project BCD_Adder.circ as structural Verilog: 4 circuits, main circuit Half Adder
module Half_Adder (
  input  A,
  input  B,
  output S,
  output C
);

  xor xor_1 (S, A, B);
  and and_1 (C, A, B);

  // Notes on the sheet:
  //   S is Sum and C is Carry and We are doing A+B
  //   Half Adder Using Mix of Gates
endmodule

module Full_Adder (
  input  A,
  input  B,
  input  C,
  output S,
  output Cout
);

  wire half_adder_1_c, half_adder_1_s, half_adder_2_c;

  Half_Adder half_adder_1 (.A(A), .B(B), .S(half_adder_1_s), .C(half_adder_1_c));
  Half_Adder half_adder_2 (.A(half_adder_1_s), .B(C), .S(S), .C(half_adder_2_c));
  or or_1 (Cout, half_adder_2_c, half_adder_1_c);

  // Notes on the sheet:
  //   Full Adder Using Two Half Adders and Mix Of Gates
  //   S is Sum and Cout is Carry and We are doing A+B+C
endmodule

module Parallel_Adder (
  input  B3,
  input  A3,
  input  B2,
  input  A2,
  input  B1,
  input  A1,
  input  B0,
  input  A0,
  input  C0,
  output Cout,
  output S3,
  output S2,
  output S1,
  output S0
);

  wire full_adder_2_cout, full_adder_3_cout, full_adder_4_cout;

  Full_Adder full_adder_1 (.A(A3), .B(B3), .C(full_adder_2_cout), .S(S3), .Cout(Cout));
  Full_Adder full_adder_2 (.A(A2), .B(B2), .C(full_adder_3_cout), .S(S2), .Cout(full_adder_2_cout));
  Full_Adder full_adder_3 (.A(A1), .B(B1), .C(full_adder_4_cout), .S(S1), .Cout(full_adder_3_cout));
  Full_Adder full_adder_4 (.A(A0), .B(B0), .C(C0), .S(S0), .Cout(full_adder_4_cout));

  // Notes on the sheet:
  //   Parallel Adder Using Full Adders
endmodule

module BCD_adder (
  input  A3,
  input  A2,
  input  A1,
  input  A0,
  input  B3,
  input  B2,
  input  B1,
  input  B0,
  input  C0,
  output Y4,
  output Y3,
  output Y2,
  output Y1,
  output Y0
);

  wire and_1_out, and_2_out, parallel_adder_1_cout, parallel_adder_1_s0, parallel_adder_1_s1,
       parallel_adder_1_s2, parallel_adder_1_s3;

  Parallel_Adder parallel_adder_1 (
    .Cout(parallel_adder_1_cout), .B3(A3), .A3(B3), .B2(A2), .A2(B2), .B1(A1), .A1(B1), .B0(A0), .A0(B0),
    .S3(parallel_adder_1_s3), .S2(parallel_adder_1_s2), .S1(parallel_adder_1_s1), .S0(parallel_adder_1_s0),
    .C0(C0));
  and and_1 (and_1_out, parallel_adder_1_s3, parallel_adder_1_s1);
  and and_2 (and_2_out, parallel_adder_1_s3, parallel_adder_1_s2);
  or or_1 (Y4, parallel_adder_1_cout, and_2_out, and_1_out);
  Parallel_Adder parallel_adder_2 (
    .B3(parallel_adder_1_s3), .A3(1'b0), .B2(parallel_adder_1_s2), .A2(Y4), .B1(parallel_adder_1_s1),
    .A1(Y4), .B0(parallel_adder_1_s0), .A0(1'b0), .S3(Y3), .S2(Y2), .S1(Y1), .S0(Y0), .C0(1'b0));  // open: Cout

  // Notes on the sheet:
  //   BCD Adder
endmodule
