// Logisim project 8-Bit Shifter.circ as structural Verilog: 6 circuits, main circuit D Flip Flop
// D-FF
module D_Flip_Flop (
  input  CLK,
  input  D,
  output Q,
  output Q_prime
);

  wire nand_1_out, nand_2_out, nand_3_out, nand_4_out;

  nand nand_1 (nand_1_out, nand_4_out, nand_2_out);
  nand nand_2 (nand_2_out, nand_1_out, CLK);
  nand nand_3 (nand_3_out, nand_2_out, CLK, nand_4_out);
  nand nand_4 (nand_4_out, nand_3_out, D);
  nand nand_5 (Q, nand_2_out, Q_prime);
  nand nand_6 (Q_prime, Q, nand_3_out);

  // Notes on the sheet:
  //   D Flip-Flop
  //   D-Flip Flop Used Here is Positive Edge Triggered
endmodule

// 8:1 MUX
module Mux (
  input  S2,
  input  S1,
  input  S0,
  input  I0,
  input  I1,
  input  I2,
  input  I3,
  input  Enable,
  input  I4,
  input  I5,
  input  I6,
  input  I7,
  output Output
);

  wire _0_out, _1_out, _2_out, _3_out, _4_out, _5_out, _6_out, _7_out, not_1_out, not_2_out, not_3_out,
       or_1_out;

  not not_1 (not_1_out, S2);
  not not_2 (not_2_out, S1);
  not not_3 (not_3_out, S0);
  and _0 (_0_out, not_3_out, not_1_out, not_2_out, I0);
  and _1 (_1_out, S0, not_2_out, not_1_out, I1);
  and _2 (_2_out, not_3_out, not_1_out, S1, I2);
  and _3 (_3_out, S1, not_1_out, S0, I3);
  and _4 (_4_out, not_3_out, S2, not_2_out, I4);
  and _5 (_5_out, S0, not_2_out, S2, I5);
  and _6 (_6_out, not_3_out, S2, S1, I6);
  and _7 (_7_out, S0, S1, S2, I7);
  or or_1 (or_1_out, _0_out, _1_out, _2_out, _3_out, _4_out, _5_out, _6_out, _7_out);
  and and_1 (Output, or_1_out, Enable);

  // Notes on the sheet:
  //   S2'S1'S0' I0 
  //   S2'S1'S0 I1 
  //   S2'S1S0' I1 
  //   S2'S1S0 I3 
  //   S2S1'S0' I4 
  //   S2S1'S0 I5
  //   S2S1S0' I06
  //   S2S1S0 I7 
  //   Assumed that Propagation Delay of Each Gate Takes Delta Unit of Time
  //   8:1 MUX using Logic Gates With 4 Delta Delay Time
endmodule

module _8_Bit_Shifter (
  input  Enable,
  input  S2,
  input  S1,
  input  S0,
  input  Left_Shift,
  input  [7:0] in_6,
  input  Right_Shift,
  output [7:0] out_8
);

  wire clock_1_out, mux_1_output, mux_2_output, mux_3_output, mux_4_output, mux_5_output, mux_6_output,
       mux_7_output, mux_8_output, not_1_out;

  Clock clock_1 (.out(clock_1_out));
  not not_1 (not_1_out, clock_1_out);
  Mux mux_1 (
    .I0(out_8[7]), .I1(out_8[6]), .I2(out_8[5]), .I3(out_8[0]), .I4(out_8[1]), .I5(out_8[6]),
    .I6(Right_Shift), .I7(in_6[7]), .Output(mux_1_output), .S2(S2), .S1(S1), .S0(S0), .Enable(Enable));
  D_Flip_Flop d_flip_flop_1 (.CLK(not_1_out), .D(mux_1_output), .Q(out_8[7]));  // open: Q_prime
  Mux mux_2 (
    .I0(out_8[6]), .I1(out_8[5]), .I2(out_8[4]), .I3(out_8[7]), .I4(out_8[0]), .I5(out_8[5]), .I6(out_8[7]),
    .I7(in_6[6]), .Output(mux_2_output), .S2(S2), .S1(S1), .S0(S0), .Enable(Enable));
  D_Flip_Flop d_flip_flop_2 (.CLK(not_1_out), .D(mux_2_output), .Q(out_8[6]));  // open: Q_prime
  Mux mux_3 (
    .I0(out_8[5]), .I1(out_8[4]), .I2(out_8[3]), .I3(out_8[6]), .I4(out_8[7]), .I5(out_8[4]), .I6(out_8[6]),
    .I7(in_6[5]), .Output(mux_3_output), .S2(S2), .S1(S1), .S0(S0), .Enable(Enable));
  D_Flip_Flop d_flip_flop_3 (.CLK(not_1_out), .D(mux_3_output), .Q(out_8[5]));  // open: Q_prime
  Mux mux_4 (
    .I0(out_8[4]), .I1(out_8[3]), .I2(out_8[2]), .I3(out_8[5]), .I4(out_8[6]), .I5(out_8[3]), .I6(out_8[5]),
    .I7(in_6[4]), .Output(mux_4_output), .S2(S2), .S1(S1), .S0(S0), .Enable(Enable));
  D_Flip_Flop d_flip_flop_4 (.CLK(not_1_out), .D(mux_4_output), .Q(out_8[4]));  // open: Q_prime
  Mux mux_5 (
    .I0(out_8[3]), .I1(out_8[2]), .I2(out_8[1]), .I3(out_8[4]), .I4(out_8[5]), .I5(out_8[2]), .I6(out_8[4]),
    .I7(in_6[3]), .Output(mux_5_output), .S2(S2), .S1(S1), .S0(S0), .Enable(Enable));
  D_Flip_Flop d_flip_flop_5 (.CLK(not_1_out), .D(mux_5_output), .Q(out_8[3]));  // open: Q_prime
  Mux mux_6 (
    .I0(out_8[2]), .I1(out_8[1]), .I2(out_8[0]), .I3(out_8[3]), .I4(out_8[4]), .I5(out_8[1]), .I6(out_8[3]),
    .I7(in_6[2]), .Output(mux_6_output), .S2(S2), .S1(S1), .S0(S0), .Enable(Enable));
  D_Flip_Flop d_flip_flop_6 (.CLK(not_1_out), .D(mux_6_output), .Q(out_8[2]));  // open: Q_prime
  Mux mux_7 (
    .I0(out_8[1]), .I1(out_8[0]), .I2(out_8[7]), .I3(out_8[2]), .I4(out_8[3]), .I5(out_8[0]), .I6(out_8[2]),
    .I7(in_6[1]), .Output(mux_7_output), .S2(S2), .S1(S1), .S0(S0), .Enable(Enable));
  D_Flip_Flop d_flip_flop_7 (.CLK(not_1_out), .D(mux_7_output), .Q(out_8[1]));  // open: Q_prime
  Mux mux_8 (
    .I0(out_8[0]), .I1(out_8[7]), .I2(out_8[6]), .I3(out_8[1]), .I4(out_8[2]), .I5(Left_Shift),
    .I6(out_8[1]), .I7(in_6[0]), .Output(mux_8_output), .S2(S2), .S1(S1), .S0(S0), .Enable(Enable));
  D_Flip_Flop d_flip_flop_8 (.CLK(not_1_out), .D(mux_8_output), .Q(out_8[0]));  // open: Q_prime

  // Notes on the sheet:
  //   8-Bit Shifter Using Splitter for Taking the Inputs
endmodule

module _2X1_MUX (
  input  I0,
  input  I1,
  input  S,
  output O
);

  wire and_1_out, and_2_out, not_1_out;

  not not_1 (not_1_out, S);
  and and_1 (and_1_out, I0, not_1_out);
  and and_2 (and_2_out, I1, S);
  or or_1 (O, and_1_out, and_2_out);

  // Notes on the sheet:
  //   2X1 MUX With 2 Delta Delay
  //   Assumed that Propagation Delay of Each Gate Takes Delta Unit of Time
endmodule

module _4X1_MUX (
  input  I3,
  input  I2,
  input  I1,
  input  I0,
  input  S0,
  input  S1,
  output O
);

  wire n2x1_mux_1_o, n2x1_mux_2_o;

  _2X1_MUX u_2x1_mux_1 (.I0(I2), .I1(I3), .O(n2x1_mux_1_o), .S(S0));
  _2X1_MUX u_2x1_mux_2 (.I0(I0), .I1(I1), .O(n2x1_mux_2_o), .S(S0));
  _2X1_MUX u_2x1_mux_3 (.I0(n2x1_mux_2_o), .I1(n2x1_mux_1_o), .O(O), .S(S1));

  // Notes on the sheet:
  //   4X1 MUX With 4 Delta Delay
endmodule

module _8X1_MUX (
  input  I7,
  input  I6,
  input  I5,
  input  I4,
  input  I3,
  input  I2,
  input  I1,
  input  I0,
  input  S2,
  input  S1,
  input  S0,
  output O
);

  wire n4x1_mux_1_o, n4x1_mux_2_o;

  _4X1_MUX u_4x1_mux_1 (.I3(I7), .I2(I6), .I1(I5), .I0(I4), .S0(S0), .S1(S1), .O(n4x1_mux_1_o));
  _4X1_MUX u_4x1_mux_2 (.I3(I3), .I2(I2), .I1(I1), .I0(I0), .S0(S0), .S1(S1), .O(n4x1_mux_2_o));
  _2X1_MUX u_2x1_mux_1 (.I0(n4x1_mux_2_o), .I1(n4x1_mux_1_o), .O(O), .S(S2));

  // Notes on the sheet:
  //   8X1 MUX With 6 Delta Delay
endmodule
