// Logisim project 3 Decade Counter.circ as structural Verilog: 3 circuits, main circuit 3-Decade BCD Counter
module T_FF (
  input  T,
  input  CLK,
  input  clear_prime,
  output Q,
  output Q_prime
);

  wire nand_1_out, nand_2_out, nand_3_out, nand_4_out, nand_5_out, nand_6_out, nand_7_out;

  nand nand_1 (nand_1_out, Q_prime, T, CLK);
  nand nand_2 (nand_2_out, CLK, T, Q);
  nand nand_3 (nand_3_out, CLK, CLK);
  nand nand_4 (nand_4_out, nand_1_out, nand_5_out);
  nand nand_5 (nand_5_out, nand_4_out, clear_prime, nand_2_out);
  nand nand_6 (nand_6_out, nand_4_out, nand_3_out);
  nand nand_7 (nand_7_out, nand_3_out, nand_5_out);
  nand nand_8 (Q, nand_6_out, Q_prime);
  nand nand_9 (Q_prime, Q, clear_prime, nand_7_out);

  // Notes on the sheet:
  //   T- Flip Flop
  //   A Negative-Edge Triggered T Flip-Flop with Active Low Clear
endmodule

module BCD (
  input  CLK,
  input  Clear,
  output A8,
  output A4,
  output A2,
  output A0
);

  wire and_1_out, and_2_out, and_3_out, and_4_out, or_1_out, t_ff_1_q_prime;

  T_FF t_ff_1 (.T(or_1_out), .CLK(CLK), .clear_prime(Clear), .Q(A8), .Q_prime(t_ff_1_q_prime));
  or or_1 (or_1_out, and_1_out, and_2_out);
  and and_1 (and_1_out, A8, A0);
  and and_2 (and_2_out, and_3_out, A4);
  T_FF t_ff_2 (.T(and_3_out), .CLK(CLK), .clear_prime(Clear), .Q(A4));  // open: Q_prime
  and and_3 (and_3_out, A0, A2);
  T_FF t_ff_3 (.T(and_4_out), .CLK(CLK), .clear_prime(Clear), .Q(A2));  // open: Q_prime
  and and_4 (and_4_out, A0, t_ff_1_q_prime);
  T_FF t_ff_4 (.T(1'b1), .CLK(CLK), .clear_prime(Clear), .Q(A0));  // open: Q_prime

  // Notes on the sheet:
  //   Decade Counter Using T Flip-Flop
endmodule

module _3_Decade_BCD_Counter (
  input  Clear,
  input  CLK,
  output Q11,
  output Q10,
  output Q9,
  output Q8,
  output Q7,
  output Q6,
  output Q5,
  output Q4,
  output Q3,
  output Q2,
  output Q1,
  output Q0
);

  wire and_1_out, and_2_out;

  BCD bcd_1 (.CLK(and_1_out), .Clear(Clear), .A8(Q11), .A4(Q10), .A2(Q9), .A0(Q8));
  and and_1 (and_1_out, Q4, and_2_out, CLK, Q7);
  BCD bcd_2 (.CLK(and_2_out), .Clear(Clear), .A8(Q7), .A4(Q6), .A2(Q5), .A0(Q4));
  and and_2 (and_2_out, Q0, CLK, Q3);
  BCD bcd_3 (.CLK(CLK), .Clear(Clear), .A8(Q3), .A4(Q2), .A2(Q1), .A0(Q0));

  // Notes on the sheet:
  //   3-Decade BCD Counter Using Decade Counter
endmodule
