// Logisim project Sequence Generator.circ as structural Verilog: 4 circuits, main circuit T Flip Flop
module T_Flip_Flop (
  input  T,
  input  CLK,
  input  clear_prime,
  output Q,
  output Q_prime
);

  wire nand_1_out, nand_2_out, nand_3_out, nand_4_out, nand_5_out, nand_6_out, nand_7_out;

  nand nand_1 (nand_1_out, Q_prime, T, CLK);
  nand nand_2 (nand_2_out, CLK, T, Q);
  nand nand_3 (nand_3_out, CLK, CLK);
  nand nand_4 (nand_4_out, nand_1_out, nand_5_out);
  nand nand_5 (nand_5_out, nand_4_out, clear_prime, nand_2_out);
  nand nand_6 (nand_6_out, nand_4_out, nand_3_out);
  nand nand_7 (nand_7_out, nand_3_out, nand_5_out);
  nand nand_8 (Q, nand_6_out, Q_prime);
  nand nand_9 (Q_prime, Q, clear_prime, nand_7_out);

  // Notes on the sheet:
  //   T- Flip Flop
  //   A Negative-Edge Triggered T Flip-Flop with Active Low Clear
endmodule

module _3X8_Decoder (
  input  S2,
  input  S1,
  input  S0,
  output Y0,
  output Y1,
  output Y2,
  output Y3,
  output Y4,
  output Y5,
  output Y6,
  output Y7
);

  wire not_1_out, not_2_out, not_3_out;

  not not_1 (not_1_out, S2);
  not not_2 (not_2_out, S1);
  not not_3 (not_3_out, S0);
  and and_1 (Y0, not_3_out, not_2_out, not_1_out);
  and and_2 (Y1, S0, not_2_out, not_1_out);
  and and_3 (Y2, not_3_out, S1, not_1_out);
  and and_4 (Y3, S0, S1, not_1_out);
  and and_5 (Y4, not_3_out, not_2_out, S2);
  and and_6 (Y5, S0, not_2_out, S2);
  and and_7 (Y6, not_3_out, S1, S2);
  and and_8 (Y7, S0, S1, S2);

  // Notes on the sheet:
  //   3X8 Decoder
endmodule

module _3_Bit_Counter (
  input  CLK,
  input  Clear_prime,
  output A2,
  output A1,
  output A0
);

  wire and_1_out;

  T_Flip_Flop t_flip_flop_1 (.T(and_1_out), .clear_prime(Clear_prime), .Q(A2), .CLK(CLK));  // open: Q_prime
  and and_1 (and_1_out, A0, A1);
  T_Flip_Flop t_flip_flop_2 (.T(A0), .clear_prime(Clear_prime), .Q(A1), .CLK(CLK));  // open: Q_prime
  T_Flip_Flop t_flip_flop_3 (.T(1'b1), .clear_prime(Clear_prime), .Q(A0), .CLK(CLK));  // open: Q_prime

  // Notes on the sheet:
  //   3-Bit Binary Counter Using T Flip Flop
endmodule

module Sequence_Generator (
  input  Clear_prime,
  output T0,
  output T1,
  output T2,
  output T3,
  output T4,
  output T5,
  output T6,
  output T7
);

  wire CLK_out, n3_bit_counter_1_a0, n3_bit_counter_1_a1, n3_bit_counter_1_a2;

  Clock CLK (.out(CLK_out));
  _3_Bit_Counter u_3_bit_counter_1 (
    .CLK(CLK_out), .Clear_prime(Clear_prime), .A2(n3_bit_counter_1_a2), .A1(n3_bit_counter_1_a1),
    .A0(n3_bit_counter_1_a0));
  _3X8_Decoder u_3x8_decoder_1 (
    .Y0(T0), .Y1(T1), .Y2(T2), .Y3(T3), .Y4(T4), .Y5(T5), .Y6(T6), .Y7(T7), .S2(n3_bit_counter_1_a2),
    .S1(n3_bit_counter_1_a1), .S0(n3_bit_counter_1_a0));

  // Notes on the sheet:
  //   Sequence Generator Using 3-Bit Binary Counter And 3X8 Decoder
endmodule
