// Logisim project Sequential Circuit.circ as structural Verilog: 19 circuits, main circuit SR Latch Using NOR Gates
module SR_Latch_Using_NOR_Gates (
  input  R,
  input  S,
  output Q,
  output Q_prime
);

  nor nor_1 (Q, R, Q_prime);
  nor nor_2 (Q_prime, Q, S);

  // Notes on the sheet:
  //   SR Latch Using NOR Gates
endmodule

module SR_Latch_Using_NAND_Gates (
  input  S,
  input  CLEAR_prime,
  input  R,
  output Q,
  output Q_prime
);

  wire nand_1_out;

  nand nand_1 (nand_1_out, S, Q_prime);
  nand nand_2 (Q_prime, nand_1_out, CLEAR_prime, R);
  and and_1 (Q, CLEAR_prime, nand_1_out);

  // Notes on the sheet:
  //   SR Latch Using NAND Gates Along With Active Low Clear
endmodule

module Clocked_RS_Flip_Flop_Using_NOR_Gates (
  input  R,
  input  CP,
  input  S,
  output Q,
  output Q_prime
);

  wire and_1_out, and_2_out;

  and and_1 (and_1_out, R, CP);
  and and_2 (and_2_out, CP, S);
  SR_Latch_Using_NOR_Gates sr_latch_using_nors_1 (.R(and_1_out), .S(and_2_out), .Q(Q), .Q_prime(Q_prime));

  // Notes on the sheet:
  //   Clocked RS Flip-Flop Using NOR Gates
  //   Level Triggered SR Flip-Flop
endmodule

module Clocked_SR_Flip_Flop_Using_NAND_Gates (
  input  S,
  input  CP,
  input  R,
  input  CLEAR_prime,
  output Q,
  output Q_prime
);

  wire nand_1_out, nand_2_out;

  nand nand_1 (nand_1_out, S, CP);
  nand nand_2 (nand_2_out, CP, R);
  SR_Latch_Using_NAND_Gates sr_latch_using_nands_1 (
    .S(nand_1_out), .R(nand_2_out), .Q(Q), .Q_prime(Q_prime), .CLEAR_prime(CLEAR_prime));

  // Notes on the sheet:
  //   Clocked RS Flip-Flop Using NAND Gates
  //   Level Triggered SR Flip-Flop
endmodule

module D_Flip_Flop (
  input  D,
  output Q,
  output Q_prime
);

  wire CP_out, not_1_out;

  not not_1 (not_1_out, D);
  Clock CP (.out(CP_out));
  Clocked_RS_Flip_Flop_Using_NOR_Gates clocked_rs_flip_flop_using_nors_1 (
    .R(not_1_out), .CP(CP_out), .S(D), .Q(Q), .Q_prime(Q_prime));

  // Notes on the sheet:
  //   Level Triggered D Flip-Flop
  //   D Flip-Flop Using Clocked RS Flip-Flop Using NOR Gates
endmodule

module T_Flip_Flop__By_MS_JK_FF (
  input  T,
  input  CP,
  input  CLEAR_prime,
  output Q,
  output Q_prime
);

  Master_Slave_JK_Flip_Flop master_slave_jk_ff_1 (
    .J(T), .CP(CP), .K(T), .CLEAR_prime(CLEAR_prime), .Q(Q), .Q_prime(Q_prime));

  // Notes on the sheet:
  //   T Flip-Flop Using Master-Slave JK Flip-Flop
endmodule

module Master_Slave_JK_Flip_Flop (
  input  J,
  input  CP,
  input  K,
  input  CLEAR_prime,
  output Q,
  output Q_prime
);

  wire nand_1_out, nand_2_out, nand_3_out, nand_4_out, nand_5_out, nand_6_out, not_1_out;

  not not_1 (not_1_out, CP);
  nand nand_1 (nand_1_out, Q_prime, J, CP);
  nand nand_2 (nand_2_out, CP, K, Q);
  nand nand_3 (nand_3_out, nand_1_out, nand_4_out);
  nand nand_4 (nand_4_out, nand_3_out, CLEAR_prime, nand_2_out);
  nand nand_5 (nand_5_out, nand_3_out, not_1_out);
  nand nand_6 (nand_6_out, not_1_out, nand_4_out);
  nand nand_7 (Q, nand_5_out, Q_prime);
  nand nand_8 (Q_prime, Q, CLEAR_prime, nand_6_out);

  // Notes on the sheet:
  //   Master-Slave JK Flip-Flop
  //   JK Flip-Flop Here is Negative-Edge Triggered and Active Low Clear
endmodule

module Binary_Ripple_Counter (
  input  in_1,
  input  CLEAR_prime,
  output A3,
  output A2,
  output A1,
  output A0
);

  T_Flip_Flop__By_MS_JK_FF t_ff_by_ms_jk_ff_1 (
    .T(1'b1), .CLEAR_prime(CLEAR_prime), .Q(A0), .CP(in_1));  // open: Q_prime
  T_Flip_Flop__By_MS_JK_FF t_ff_by_ms_jk_ff_2 (.T(1'b1), .CLEAR_prime(CLEAR_prime), .Q(A1), .CP(A0));  // open: Q_prime
  T_Flip_Flop__By_MS_JK_FF t_ff_by_ms_jk_ff_3 (.T(1'b1), .CLEAR_prime(CLEAR_prime), .Q(A2), .CP(A1));  // open: Q_prime
  T_Flip_Flop__By_MS_JK_FF t_ff_by_ms_jk_ff_4 (.T(1'b1), .CLEAR_prime(CLEAR_prime), .Q(A3), .CP(A2));  // open: Q_prime

  // Notes on the sheet:
  //   Binary Ripple Counter
endmodule

module D_Flip_Flop__Using_Clocked_SR_NAND_with_CLR (
  input  D,
  input  CP,
  input  CLEAR_prime,
  output Q,
  output Q_prime
);

  wire not_1_out;

  not not_1 (not_1_out, D);
  Clocked_SR_Flip_Flop_Using_NAND_Gates clocked_sr_flip_flop_using_nands_1 (
    .S(D), .R(not_1_out), .Q(Q), .Q_prime(Q_prime), .CP(CP), .CLEAR_prime(CLEAR_prime));

  // Notes on the sheet:
  //   D Flip-Flop Using Clocked SR Flip-Flop Using NAND Gates
  //   Level Triggered D Flip-Flop With Active Low Clear
endmodule

module _4_Bit_Register_With_Parallel_Load_using_D_FF (
  input  LOAD,
  input  I3,
  input  I2,
  input  I1,
  input  I0,
  input  CP,
  input  CLEAR_prime,
  output A3,
  output A2,
  output A1,
  output A0
);

  wire and_1_out, and_2_out, and_3_out, and_4_out, and_5_out, and_6_out, and_7_out, and_8_out, not_1_out,
       or_1_out, or_2_out, or_3_out, or_4_out;

  not not_1 (not_1_out, LOAD);
  and and_1 (and_1_out, LOAD, I3);
  and and_2 (and_2_out, LOAD, I2);
  and and_3 (and_3_out, LOAD, I1);
  and and_4 (and_4_out, LOAD, I0);
  and and_5 (and_5_out, A3, not_1_out);
  and and_6 (and_6_out, A2, not_1_out);
  and and_7 (and_7_out, A1, not_1_out);
  and and_8 (and_8_out, A0, not_1_out);
  or or_1 (or_1_out, and_5_out, and_1_out);
  or or_2 (or_2_out, and_6_out, and_2_out);
  or or_3 (or_3_out, and_7_out, and_3_out);
  or or_4 (or_4_out, and_8_out, and_4_out);
  D_Flip_Flop__Using_Clocked_SR_NAND_with_CLR d_ff_using_clocked_sr_nand_with_clr_1 (
    .D(or_1_out), .CLEAR_prime(CLEAR_prime), .Q(A3), .CP(CP));  // open: Q_prime
  D_Flip_Flop__Using_Clocked_SR_NAND_with_CLR d_ff_using_clocked_sr_nand_with_clr_2 (
    .D(or_2_out), .CLEAR_prime(CLEAR_prime), .Q(A2), .CP(CP));  // open: Q_prime
  D_Flip_Flop__Using_Clocked_SR_NAND_with_CLR d_ff_using_clocked_sr_nand_with_clr_3 (
    .D(or_3_out), .CLEAR_prime(CLEAR_prime), .Q(A1), .CP(CP));  // open: Q_prime
  D_Flip_Flop__Using_Clocked_SR_NAND_with_CLR d_ff_using_clocked_sr_nand_with_clr_4 (
    .D(or_4_out), .CLEAR_prime(CLEAR_prime), .Q(A0), .CP(CP));  // open: Q_prime

  // Notes on the sheet:
  //   4-Bit Register With Parallel Load Using D Flip-Flop
endmodule

module D_Flip_Flop__By_MS_JK_FF (
  input  D,
  input  CP,
  input  CLEAR_prime,
  output Q,
  output Q_prime
);

  wire not_1_out;

  not not_1 (not_1_out, D);
  Master_Slave_JK_Flip_Flop master_slave_jk_ff_1 (
    .J(D), .CP(CP), .K(not_1_out), .CLEAR_prime(CLEAR_prime), .Q(Q), .Q_prime(Q_prime));

  // Notes on the sheet:
  //   D Flip-Flop Using Master Slave JK Flip-Flop
  //   D Flip-Flop Here is Negative-Edge Triggered and Active Low Clear
endmodule

module Memory_Cell (
  input  SELECT,
  input  INPUT,
  input  CP,
  input  CLEAR_prime,
  input  READ_WRITE,
  output Y
);

  wire and_1_out, and_2_out, master_slave_jk_ff_1_q, not_1_out, not_2_out;

  not not_1 (not_1_out, INPUT);
  and and_1 (and_1_out, SELECT, not_2_out, INPUT);
  and and_2 (and_2_out, SELECT, not_2_out, not_1_out);
  not not_2 (not_2_out, READ_WRITE);
  Master_Slave_JK_Flip_Flop master_slave_jk_ff_1 (
    .J(and_1_out), .CP(CP), .K(and_2_out), .CLEAR_prime(CLEAR_prime), .Q(master_slave_jk_ff_1_q));  // open: Q_prime
  and and_3 (Y, SELECT, master_slave_jk_ff_1_q, READ_WRITE);

  // Notes on the sheet:
  //   Memory Cell
  //   JK Flip-Flop Here is Negative-Edge Triggered and Active Low Clear
endmodule

module BCD_Ripple_Counter__Decade_Counter (
  input  CP,
  input  CLEAR_prime,
  output Q8,
  output Q4,
  output Q2,
  output Q1
);

  wire and_1_out, master_slave_jk_ff_4_q_prime;

  Master_Slave_JK_Flip_Flop master_slave_jk_ff_1 (
    .J(1'b1), .CP(CP), .K(1'b1), .CLEAR_prime(CLEAR_prime), .Q(Q1));  // open: Q_prime
  Master_Slave_JK_Flip_Flop master_slave_jk_ff_2 (
    .J(master_slave_jk_ff_4_q_prime), .CP(Q1), .K(1'b1), .CLEAR_prime(CLEAR_prime), .Q(Q2));  // open: Q_prime
  Master_Slave_JK_Flip_Flop master_slave_jk_ff_3 (
    .J(1'b1), .CP(Q2), .K(1'b1), .CLEAR_prime(CLEAR_prime), .Q(Q4));  // open: Q_prime
  and and_1 (and_1_out, Q4, Q2);
  Master_Slave_JK_Flip_Flop master_slave_jk_ff_4 (
    .J(and_1_out), .CP(Q1), .K(1'b1), .CLEAR_prime(CLEAR_prime), .Q(Q8),
    .Q_prime(master_slave_jk_ff_4_q_prime));

  // Notes on the sheet:
  //   BCD Ripple Counter (Decade Counter)
endmodule

module _4_Bit_Up_Down_Binary_Counter (
  input  CLEAR_prime,
  input  CP,
  input  UP,
  input  DOWN,
  output A3,
  output A3_prime,
  output A2,
  output A2_prime,
  output A1,
  output A1_prime,
  output A0,
  output A0_prime
);

  wire and_1_out, and_2_out, and_3_out, and_4_out, and_5_out, and_6_out, and_7_out, and_8_out, not_1_out,
       not_2_out, or_1_out, or_2_out, or_3_out, or_4_out;

  T_Flip_Flop__By_MS_JK_FF t_ff_by_ms_jk_ff_1 (
    .T(or_1_out), .CLEAR_prime(CLEAR_prime), .Q(A3), .Q_prime(A3_prime), .CP(CP));
  or or_1 (or_1_out, and_2_out, and_1_out);
  and and_1 (and_1_out, A2, and_3_out);
  and and_2 (and_2_out, A2_prime, and_4_out);
  T_Flip_Flop__By_MS_JK_FF t_ff_by_ms_jk_ff_2 (
    .T(or_2_out), .CLEAR_prime(CLEAR_prime), .Q(A2), .Q_prime(A2_prime), .CP(CP));
  or or_2 (or_2_out, and_4_out, and_3_out);
  and and_3 (and_3_out, A1, and_5_out);
  and and_4 (and_4_out, A1_prime, and_6_out);
  T_Flip_Flop__By_MS_JK_FF t_ff_by_ms_jk_ff_3 (
    .T(or_3_out), .CLEAR_prime(CLEAR_prime), .Q(A1), .Q_prime(A1_prime), .CP(CP));
  or or_3 (or_3_out, and_6_out, and_5_out);
  and and_5 (and_5_out, A0, and_7_out);
  and and_6 (and_6_out, A0_prime, and_8_out);
  T_Flip_Flop__By_MS_JK_FF t_ff_by_ms_jk_ff_4 (
    .T(or_4_out), .CLEAR_prime(CLEAR_prime), .Q(A0), .Q_prime(A0_prime), .CP(CP));
  or or_4 (or_4_out, and_8_out, and_7_out);
  and and_7 (and_7_out, UP, not_1_out);
  and and_8 (and_8_out, not_2_out, DOWN);
  not not_1 (not_1_out, DOWN);
  not not_2 (not_2_out, UP);

  // Notes on the sheet:
  //   4-Bit Up Down Binary Counter
endmodule

module Binary_Counter_with_Parallel_Load (
  input  COUNT,
  input  LOAD,
  input  I3,
  input  I2,
  input  I1,
  input  I0,
  input  CP,
  input  CLEAR_prime,
  output A0,
  output A1,
  output A2,
  output A3,
  output CARRY_OUT
);

  wire and_1_out, and_2_out, and_3_out, and_4_out, and_5_out, and_6_out, and_7_out, and_8_out, and_9_out,
       and_10_out, and_11_out, and_12_out, not_1_out, not_2_out, not_3_out, not_4_out, not_5_out, not_6_out,
       or_1_out, or_2_out, or_3_out, or_4_out, or_5_out, or_6_out, or_7_out, or_8_out;

  not not_1 (not_1_out, LOAD);
  not not_2 (not_2_out, not_1_out);
  and and_1 (and_1_out, COUNT, not_1_out);
  not not_3 (not_3_out, I3);
  not not_4 (not_4_out, I2);
  not not_5 (not_5_out, I1);
  not not_6 (not_6_out, I0);
  and and_2 (and_2_out, A0, and_1_out);
  and and_3 (and_3_out, A1, A0, and_1_out);
  and and_4 (and_4_out, A2, A1, A0, and_1_out);
  and and_5 (and_5_out, I3, not_2_out);
  and and_6 (and_6_out, not_3_out, not_2_out);
  and and_7 (and_7_out, I2, not_2_out);
  and and_8 (and_8_out, not_4_out, not_2_out);
  and and_9 (and_9_out, I1, not_2_out);
  and and_10 (and_10_out, not_5_out, not_2_out);
  and and_11 (and_11_out, I0, not_2_out);
  and and_12 (and_12_out, not_6_out, not_2_out);
  or or_1 (or_1_out, and_5_out, and_1_out);
  or or_2 (or_2_out, and_1_out, and_6_out);
  or or_3 (or_3_out, and_7_out, and_2_out);
  or or_4 (or_4_out, and_2_out, and_8_out);
  or or_5 (or_5_out, and_9_out, and_3_out);
  or or_6 (or_6_out, and_3_out, and_10_out);
  or or_7 (or_7_out, and_11_out, and_4_out);
  or or_8 (or_8_out, and_4_out, and_12_out);
  and and_13 (CARRY_OUT, A3, A2, A1, A0, and_1_out);
  Master_Slave_JK_Flip_Flop master_slave_jk_ff_1 (
    .J(or_1_out), .CP(CP), .K(or_2_out), .CLEAR_prime(CLEAR_prime), .Q(A0));  // open: Q_prime
  Master_Slave_JK_Flip_Flop master_slave_jk_ff_2 (
    .J(or_3_out), .CP(CP), .K(or_4_out), .CLEAR_prime(CLEAR_prime), .Q(A1));  // open: Q_prime
  Master_Slave_JK_Flip_Flop master_slave_jk_ff_3 (
    .J(or_5_out), .CP(CP), .K(or_6_out), .CLEAR_prime(CLEAR_prime), .Q(A2));  // open: Q_prime
  Master_Slave_JK_Flip_Flop master_slave_jk_ff_4 (
    .J(or_7_out), .CP(CP), .K(or_8_out), .CLEAR_prime(CLEAR_prime), .Q(A3));  // open: Q_prime

  // Notes on the sheet:
  //   Binary Counter With Parallel Load
  //   JK Flip-Flop Here is Negative-Edge Triggered and Active Low Clear
endmodule

module MS_JK_Flip_Flop__Positive_Edge_Triggered (
  input  J,
  input  CP,
  input  K,
  input  CLEAR_prime,
  output Q,
  output Q_prime
);

  wire nand_1_out, nand_2_out, nand_3_out, nand_4_out, nand_5_out, nand_6_out, not_1_out;

  not not_1 (not_1_out, CP);
  nand nand_1 (nand_1_out, Q_prime, J, not_1_out);
  nand nand_2 (nand_2_out, not_1_out, K, Q);
  nand nand_3 (nand_3_out, nand_1_out, nand_4_out);
  nand nand_4 (nand_4_out, nand_3_out, CLEAR_prime, nand_2_out);
  nand nand_5 (nand_5_out, nand_3_out, CP);
  nand nand_6 (nand_6_out, CP, nand_4_out);
  nand nand_7 (Q, nand_5_out, Q_prime);
  nand nand_8 (Q_prime, Q, CLEAR_prime, nand_6_out);

  // Notes on the sheet:
  //   Master-Slave JK Flip-Flop
  //   JK Flip-Flop Here is Positive-Edge Triggered and Active Low Clear
endmodule

module Memory_Organisation (
  input  I4,
  input  I3,
  input  I2,
  input  I1,
  input  I0,
  input  S1,
  input  S0,
  input  CP,
  input  Clear_prime,
  input  READ_WRITE,
  output Y4,
  output Y3,
  output Y2,
  output Y1,
  output Y0
);

  wire memory_cell_1_y, memory_cell_2_y, memory_cell_3_y, memory_cell_4_y, memory_cell_5_y, memory_cell_6_y,
       memory_cell_7_y, memory_cell_8_y, memory_cell_9_y, memory_cell_10_y, memory_cell_11_y,
       memory_cell_12_y, memory_cell_13_y, memory_cell_14_y, memory_cell_15_y, memory_cell_16_y,
       memory_cell_17_y, memory_cell_18_y, memory_cell_19_y, memory_cell_20_y, n2x4_decoder_1_y0,
       n2x4_decoder_1_y1, n2x4_decoder_1_y2, n2x4_decoder_1_y3;

  _2X4_Decoder u_2x4_decoder_1 (
    .S1(S1), .S0(S0), .Y0(n2x4_decoder_1_y0), .Y1(n2x4_decoder_1_y1), .Y2(n2x4_decoder_1_y2),
    .Y3(n2x4_decoder_1_y3));
  Memory_Cell memory_cell_1 (
    .INPUT(I4), .CP(CP), .CLEAR_prime(Clear_prime), .Y(memory_cell_1_y), .SELECT(n2x4_decoder_1_y0),
    .READ_WRITE(READ_WRITE));
  Memory_Cell memory_cell_2 (
    .INPUT(I4), .CP(CP), .CLEAR_prime(Clear_prime), .Y(memory_cell_2_y), .SELECT(n2x4_decoder_1_y1),
    .READ_WRITE(READ_WRITE));
  Memory_Cell memory_cell_3 (
    .INPUT(I4), .CP(CP), .CLEAR_prime(Clear_prime), .Y(memory_cell_3_y), .SELECT(n2x4_decoder_1_y2),
    .READ_WRITE(READ_WRITE));
  Memory_Cell memory_cell_4 (
    .INPUT(I4), .CP(CP), .CLEAR_prime(Clear_prime), .Y(memory_cell_4_y), .SELECT(n2x4_decoder_1_y3),
    .READ_WRITE(READ_WRITE));
  or or_1 (Y4, memory_cell_4_y, memory_cell_3_y, memory_cell_2_y, memory_cell_1_y);
  Memory_Cell memory_cell_5 (
    .INPUT(I3), .CP(CP), .CLEAR_prime(Clear_prime), .Y(memory_cell_5_y), .SELECT(n2x4_decoder_1_y0),
    .READ_WRITE(READ_WRITE));
  Memory_Cell memory_cell_6 (
    .INPUT(I3), .CP(CP), .CLEAR_prime(Clear_prime), .Y(memory_cell_6_y), .SELECT(n2x4_decoder_1_y1),
    .READ_WRITE(READ_WRITE));
  Memory_Cell memory_cell_7 (
    .INPUT(I3), .CP(CP), .CLEAR_prime(Clear_prime), .Y(memory_cell_7_y), .SELECT(n2x4_decoder_1_y2),
    .READ_WRITE(READ_WRITE));
  Memory_Cell memory_cell_8 (
    .INPUT(I3), .CP(CP), .CLEAR_prime(Clear_prime), .Y(memory_cell_8_y), .SELECT(n2x4_decoder_1_y3),
    .READ_WRITE(READ_WRITE));
  or or_2 (Y3, memory_cell_8_y, memory_cell_7_y, memory_cell_6_y, memory_cell_5_y);
  Memory_Cell memory_cell_9 (
    .INPUT(I2), .CP(CP), .CLEAR_prime(Clear_prime), .Y(memory_cell_9_y), .SELECT(n2x4_decoder_1_y0),
    .READ_WRITE(READ_WRITE));
  Memory_Cell memory_cell_10 (
    .INPUT(I2), .CP(CP), .CLEAR_prime(Clear_prime), .Y(memory_cell_10_y), .SELECT(n2x4_decoder_1_y1),
    .READ_WRITE(READ_WRITE));
  Memory_Cell memory_cell_11 (
    .INPUT(I2), .CP(CP), .CLEAR_prime(Clear_prime), .Y(memory_cell_11_y), .SELECT(n2x4_decoder_1_y2),
    .READ_WRITE(READ_WRITE));
  Memory_Cell memory_cell_12 (
    .INPUT(I2), .CP(CP), .CLEAR_prime(Clear_prime), .Y(memory_cell_12_y), .SELECT(n2x4_decoder_1_y3),
    .READ_WRITE(READ_WRITE));
  or or_3 (Y2, memory_cell_12_y, memory_cell_11_y, memory_cell_10_y, memory_cell_9_y);
  Memory_Cell memory_cell_13 (
    .INPUT(I1), .CP(CP), .CLEAR_prime(Clear_prime), .Y(memory_cell_13_y), .SELECT(n2x4_decoder_1_y0),
    .READ_WRITE(READ_WRITE));
  Memory_Cell memory_cell_14 (
    .INPUT(I1), .CP(CP), .CLEAR_prime(Clear_prime), .Y(memory_cell_14_y), .SELECT(n2x4_decoder_1_y1),
    .READ_WRITE(READ_WRITE));
  Memory_Cell memory_cell_15 (
    .INPUT(I1), .CP(CP), .CLEAR_prime(Clear_prime), .Y(memory_cell_15_y), .SELECT(n2x4_decoder_1_y2),
    .READ_WRITE(READ_WRITE));
  Memory_Cell memory_cell_16 (
    .INPUT(I1), .CP(CP), .CLEAR_prime(Clear_prime), .Y(memory_cell_16_y), .SELECT(n2x4_decoder_1_y3),
    .READ_WRITE(READ_WRITE));
  or or_4 (Y1, memory_cell_16_y, memory_cell_15_y, memory_cell_14_y, memory_cell_13_y);
  Memory_Cell memory_cell_17 (
    .INPUT(I0), .CP(CP), .CLEAR_prime(Clear_prime), .Y(memory_cell_17_y), .SELECT(n2x4_decoder_1_y0),
    .READ_WRITE(READ_WRITE));
  Memory_Cell memory_cell_18 (
    .INPUT(I0), .CP(CP), .CLEAR_prime(Clear_prime), .Y(memory_cell_18_y), .SELECT(n2x4_decoder_1_y1),
    .READ_WRITE(READ_WRITE));
  Memory_Cell memory_cell_19 (
    .INPUT(I0), .CP(CP), .CLEAR_prime(Clear_prime), .Y(memory_cell_19_y), .SELECT(n2x4_decoder_1_y2),
    .READ_WRITE(READ_WRITE));
  Memory_Cell memory_cell_20 (
    .INPUT(I0), .CP(CP), .CLEAR_prime(Clear_prime), .Y(memory_cell_20_y), .SELECT(n2x4_decoder_1_y3),
    .READ_WRITE(READ_WRITE));
  or or_5 (Y0, memory_cell_20_y, memory_cell_19_y, memory_cell_18_y, memory_cell_17_y);

  // Notes on the sheet:
  //   Clear is Low Active
  //   Clock is Negative-Edge Triggered
  //   1 For READ And 0 For Write
  //   Memory Organisation
  //   Data Inputs
  //   Data Outputs
endmodule

module _1X2_Decoder (
  input  S,
  input  E,
  output Y0,
  output Y1
);

  wire not_1_out, not_2_out;

  not not_1 (not_1_out, S);
  not not_2 (not_2_out, E);
  and and_1 (Y0, not_1_out, not_2_out);
  and and_2 (Y1, not_2_out, S);

  // Notes on the sheet:
  //   1X2 Decoder
  //   S is Select Line and E is Enable which is Low Active Here
endmodule

module _2X4_Decoder (
  input  S1,
  input  S0,
  output Y0,
  output Y1,
  output Y2,
  output Y3
);

  wire not_1_out;

  not not_1 (not_1_out, S1);
  _1X2_Decoder u_1x2_decoder_1 (.S(S0), .Y0(Y0), .Y1(Y1), .E(S1));
  _1X2_Decoder u_1x2_decoder_2 (.S(S0), .Y0(Y2), .Y1(Y3), .E(not_1_out));

  // Notes on the sheet:
  //   2X4 Decoder Using 1x2 Decoder
endmodule
